// Logisim project Darkstar.circ as structural Verilog
module ALU (
  input  [2:0] ALU_Op,
  input  ADD0_SUB1_SRL0_SRA1,
  input  [31:0] A,
  input  [31:0] B,
  output L,
  output LU,
  output EQ,
  output NEQ,
  output GE,
  output GEU,
  output [31:0] Res
);

  wire [31:0] adder_1_out, and_1_out, bit_extender_1_out, bit_extender_2_out, multiplexer_1_out,
       multiplexer_2_out, negator_1_out, or_1_out, shifter_1_out, shifter_2_out, shifter_3_out, xor_1_out;

  Negator #(.width(32)) negator_1 (.in(B), .out(negator_1_out));
  Multiplexer #(.width(32)) multiplexer_1 (
    .in0(B), .in1(negator_1_out), .out(multiplexer_1_out), .sel(ADD0_SUB1_SRL0_SRA1));
  Adder #(.width(32)) adder_1 (.a(A), .b(multiplexer_1_out), .out(adder_1_out), .cin(1'b0));  // open: cout
  Shifter #(.width(32)) shifter_1 (.in(A), .\dist (B[4:0]), .out(shifter_1_out));
  Comparator #(.width(32)) comparator_1 (.a(A), .b(B), .eq(EQ), .lt(L));  // open: gt
  Comparator #(.mode("unsigned"), .width(32)) comparator_2 (.a(A), .b(B), .lt(LU));  // open: gt, eq
  Shifter #(.shift("lr"), .width(32)) shifter_2 (.in(A), .\dist (B[4:0]), .out(shifter_2_out));
  Shifter #(.shift("ar"), .width(32)) shifter_3 (.in(A), .\dist (B[4:0]), .out(shifter_3_out));
  assign or_1_out = A | B;  // OR_Gate or_1, 32 bits wide
  assign and_1_out = A & B;  // AND_Gate and_1, 32 bits wide
  assign xor_1_out = A ^ B;  // XOR_Gate xor_1, 32 bits wide
  Multiplexer #(.width(32)) multiplexer_2 (
    .in0(shifter_2_out), .in1(shifter_3_out), .out(multiplexer_2_out), .sel(ADD0_SUB1_SRL0_SRA1));
  assign bit_extender_1_out = {{31{1'b0}}, L};  // Bit_Extender bit_extender_1
  assign bit_extender_2_out = {{31{1'b0}}, LU};  // Bit_Extender bit_extender_2
  not not_1 (NEQ, EQ);
  not not_2 (GE, L);
  not not_3 (GEU, LU);
  Multiplexer #(.select(3), .width(32)) multiplexer_3 (
    .in0(adder_1_out), .in1(shifter_1_out), .in2(bit_extender_1_out), .in3(bit_extender_2_out),
    .in4(xor_1_out), .in5(multiplexer_2_out), .in6(or_1_out), .in7(and_1_out), .out(Res), .sel(ALU_Op));

  // Notes on the sheet:
  //   110 = OR
  //   111 = AND
  //   Opcodes
  //   000 = ADD / SUB
  //   001 = SLL (Shift Left Logical)
  //   010 = SLT (Set if Less Than)
  //   100 = XOR (Exclusive OR)
  //   011 = SLTU (Set if Less Than (Unsigned))
  //   101 = SRL (Shift Right Logical) / SRA (Shift Right Arithmetic)
endmodule

module Regfile (
  input  [4:0] Read_Register1,
  input  [4:0] Read_Register2,
  input  [31:0] Write_Data,
  input  Clock,
  input  Reset,
  input  [4:0] Write_Register,
  input  Write_Enable,
  input  [31:0] PC_In,
  output [31:0] Reg1_Out,
  output [31:0] Reg2_Out,
  output [31:0] PC_Out
);

  wire decoder_1_out1, decoder_1_out2, decoder_1_out3, decoder_1_out4, decoder_1_out5, decoder_1_out6,
       decoder_1_out7, decoder_1_out8, decoder_1_out9, decoder_1_out10, decoder_1_out11, decoder_1_out12,
       decoder_1_out13, decoder_1_out14, decoder_1_out15, decoder_1_out16, decoder_1_out17, decoder_1_out18,
       decoder_1_out19, decoder_1_out20, decoder_1_out21, decoder_1_out22, decoder_1_out23, decoder_1_out24,
       decoder_1_out25, decoder_1_out26, decoder_1_out27, decoder_1_out28, decoder_1_out29, decoder_1_out30,
       decoder_1_out31;
  wire [31:0] x0_q, x1_q, x2_q, x3_q, x4_q, x5_q, x6_q, x7_q, x8_q, x9_q, x10_q, x11_q, x12_q, x13_q, x14_q,
       x15_q, x16_q, x17_q, x18_q, x19_q, x20_q, x21_q, x22_q, x23_q, x24_q, x25_q, x26_q, x27_q, x28_q,
       x29_q, x30_q, x31_q;

  Decoder #(.select(5)) decoder_1 (
    .out1(decoder_1_out1), .out2(decoder_1_out2), .out3(decoder_1_out3), .out4(decoder_1_out4),
    .out5(decoder_1_out5), .out6(decoder_1_out6), .out7(decoder_1_out7), .out8(decoder_1_out8),
    .out9(decoder_1_out9), .out10(decoder_1_out10), .out11(decoder_1_out11), .out12(decoder_1_out12),
    .out13(decoder_1_out13), .out14(decoder_1_out14), .out15(decoder_1_out15), .out16(decoder_1_out16),
    .out17(decoder_1_out17), .out18(decoder_1_out18), .out19(decoder_1_out19), .out20(decoder_1_out20),
    .out21(decoder_1_out21), .out22(decoder_1_out22), .out23(decoder_1_out23), .out24(decoder_1_out24),
    .out25(decoder_1_out25), .out26(decoder_1_out26), .out27(decoder_1_out27), .out28(decoder_1_out28),
    .out29(decoder_1_out29), .out30(decoder_1_out30), .out31(decoder_1_out31), .sel(Write_Register),
    .en(Write_Enable));  // open: out0
  Register #(.width(32)) x0 (.D(Write_Data), .en(1'b0), .clk(Clock), .Q(x0_q), .clr(Reset));
  Register #(.width(32)) x1 (.D(Write_Data), .en(decoder_1_out1), .clk(Clock), .Q(x1_q), .clr(Reset));
  Register #(.width(32)) x2 (.D(Write_Data), .en(decoder_1_out2), .clk(Clock), .Q(x2_q), .clr(Reset));
  Register #(.width(32)) x3 (.D(Write_Data), .en(decoder_1_out3), .clk(Clock), .Q(x3_q), .clr(Reset));
  Register #(.width(32)) x4 (.D(Write_Data), .en(decoder_1_out4), .clk(Clock), .Q(x4_q), .clr(Reset));
  Register #(.width(32)) x5 (.D(Write_Data), .en(decoder_1_out5), .clk(Clock), .Q(x5_q), .clr(Reset));
  Register #(.width(32)) x6 (.D(Write_Data), .en(decoder_1_out6), .clk(Clock), .Q(x6_q), .clr(Reset));
  Register #(.width(32)) x7 (.D(Write_Data), .en(decoder_1_out7), .clk(Clock), .Q(x7_q), .clr(Reset));
  Register #(.width(32)) x8 (.D(Write_Data), .en(decoder_1_out8), .clk(Clock), .Q(x8_q), .clr(Reset));
  Register #(.width(32)) x9 (.D(Write_Data), .en(decoder_1_out9), .clk(Clock), .Q(x9_q), .clr(Reset));
  Register #(.width(32)) x10 (.D(Write_Data), .en(decoder_1_out10), .clk(Clock), .Q(x10_q), .clr(Reset));
  Register #(.width(32)) x11 (.D(Write_Data), .en(decoder_1_out11), .clk(Clock), .Q(x11_q), .clr(Reset));
  Register #(.width(32)) x12 (.D(Write_Data), .en(decoder_1_out12), .clk(Clock), .Q(x12_q), .clr(Reset));
  Register #(.width(32)) x13 (.D(Write_Data), .en(decoder_1_out13), .clk(Clock), .Q(x13_q), .clr(Reset));
  Register #(.width(32)) x14 (.D(Write_Data), .en(decoder_1_out14), .clk(Clock), .Q(x14_q), .clr(Reset));
  Register #(.width(32)) x15 (.D(Write_Data), .en(decoder_1_out15), .clk(Clock), .Q(x15_q), .clr(Reset));
  Register #(.width(32)) x16 (.D(Write_Data), .en(decoder_1_out16), .clk(Clock), .Q(x16_q), .clr(Reset));
  Register #(.width(32)) x17 (.D(Write_Data), .en(decoder_1_out17), .clk(Clock), .Q(x17_q), .clr(Reset));
  Register #(.width(32)) x18 (.D(Write_Data), .en(decoder_1_out18), .clk(Clock), .Q(x18_q), .clr(Reset));
  Register #(.width(32)) x19 (.D(Write_Data), .en(decoder_1_out19), .clk(Clock), .Q(x19_q), .clr(Reset));
  Register #(.width(32)) x20 (.D(Write_Data), .en(decoder_1_out20), .clk(Clock), .Q(x20_q), .clr(Reset));
  Register #(.width(32)) x21 (.D(Write_Data), .en(decoder_1_out21), .clk(Clock), .Q(x21_q), .clr(Reset));
  Register #(.width(32)) x22 (.D(Write_Data), .en(decoder_1_out22), .clk(Clock), .Q(x22_q), .clr(Reset));
  Register #(.width(32)) x23 (.D(Write_Data), .en(decoder_1_out23), .clk(Clock), .Q(x23_q), .clr(Reset));
  Register #(.width(32)) x24 (.D(Write_Data), .en(decoder_1_out24), .clk(Clock), .Q(x24_q), .clr(Reset));
  Register #(.width(32)) x25 (.D(Write_Data), .en(decoder_1_out25), .clk(Clock), .Q(x25_q), .clr(Reset));
  Register #(.width(32)) x26 (.D(Write_Data), .en(decoder_1_out26), .clk(Clock), .Q(x26_q), .clr(Reset));
  Register #(.width(32)) x27 (.D(Write_Data), .en(decoder_1_out27), .clk(Clock), .Q(x27_q), .clr(Reset));
  Register #(.width(32)) x28 (.D(Write_Data), .en(decoder_1_out28), .clk(Clock), .Q(x28_q), .clr(Reset));
  Register #(.width(32)) x29 (.D(Write_Data), .en(decoder_1_out29), .clk(Clock), .Q(x29_q), .clr(Reset));
  Register #(.width(32)) x30 (.D(Write_Data), .en(decoder_1_out30), .clk(Clock), .Q(x30_q), .clr(Reset));
  Register #(.width(32)) x31 (.D(Write_Data), .en(decoder_1_out31), .clk(Clock), .Q(x31_q), .clr(Reset));
  Register #(.width(32)) pc (.D(PC_In), .en(1'b1), .clk(Clock), .Q(PC_Out), .clr(Reset));
  Multiplexer #(.select(5), .width(32)) multiplexer_1 (
    .in0(x0_q), .in1(x1_q), .in2(x2_q), .in3(x3_q), .in4(x4_q), .in5(x5_q), .in6(x6_q), .in7(x7_q),
    .in8(x8_q), .in9(x9_q), .in10(x10_q), .in11(x11_q), .in12(x12_q), .in13(x13_q), .in14(x14_q),
    .in15(x15_q), .in16(x16_q), .in17(x17_q), .in18(x18_q), .in19(x19_q), .in20(x20_q), .in21(x21_q),
    .in22(x22_q), .in23(x23_q), .in24(x24_q), .in25(x25_q), .in26(x26_q), .in27(x27_q), .in28(x28_q),
    .in29(x29_q), .in30(x30_q), .in31(x31_q), .out(Reg1_Out), .sel(Read_Register1));
  Multiplexer #(.select(5), .width(32)) multiplexer_2 (
    .in0(x0_q), .in1(x1_q), .in2(x2_q), .in3(x3_q), .in4(x4_q), .in5(x5_q), .in6(x6_q), .in7(x7_q),
    .in8(x8_q), .in9(x9_q), .in10(x10_q), .in11(x11_q), .in12(x12_q), .in13(x13_q), .in14(x14_q),
    .in15(x15_q), .in16(x16_q), .in17(x17_q), .in18(x18_q), .in19(x19_q), .in20(x20_q), .in21(x21_q),
    .in22(x22_q), .in23(x23_q), .in24(x24_q), .in25(x25_q), .in26(x26_q), .in27(x27_q), .in28(x28_q),
    .in29(x29_q), .in30(x30_q), .in31(x31_q), .out(Reg2_Out), .sel(Read_Register2));
endmodule

module Memory (
  input  Unsigned0_Signed1,
  input  [31:0] Address,
  input  Store,
  input  Load,
  input  Clock,
  input  [31:0] Data_In,
  input  [1:0] Size_Flag,
  output [31:0] Data_Out
);

  wire decoder_1_out0, decoder_1_out1, decoder_1_out2, decoder_1_out3, decoder_1_out4, decoder_1_out5,
       decoder_1_out6, decoder_1_out7, decoder_1_out8, decoder_1_out9, decoder_1_out10, decoder_1_out11,
       decoder_1_out12, decoder_1_out13, decoder_1_out14, decoder_1_out15, or_1_out;
  wire [31:0] RAM0_data_out, RAM1_data_out, RAM2_data_out, RAM3_data_out, RAM4_data_out, RAM5_data_out,
       RAM6_data_out, RAM7_data_out, RAM8_data_out, RAM9_data_out, RAM10_data_out, RAM11_data_out,
       RAM12_data_out, RAM13_data_out, RAM14_data_out, RAM15_data_out;

  or or_1 (or_1_out, Store, Load);
  Decoder #(.select(4)) decoder_1 (
    .out0(decoder_1_out0), .out1(decoder_1_out1), .out2(decoder_1_out2), .out3(decoder_1_out3),
    .out4(decoder_1_out4), .out5(decoder_1_out5), .out6(decoder_1_out6), .out7(decoder_1_out7),
    .out8(decoder_1_out8), .out9(decoder_1_out9), .out10(decoder_1_out10), .out11(decoder_1_out11),
    .out12(decoder_1_out12), .out13(decoder_1_out13), .out14(decoder_1_out14), .out15(decoder_1_out15),
    .sel(Address[27:24]), .en(or_1_out));
  RAM_Block RAM0 (
    .Unsigned0_Signed1(Unsigned0_Signed1), .Enable(decoder_1_out0), .Load(Load), .Store(Store),
    .Size_Flag(Size_Flag), .Address(Address[23:0]), .Clock(Clock), .Data_In(Data_In), .Data_Out(RAM0_data_out));
  RAM_Block RAM1 (
    .Unsigned0_Signed1(Unsigned0_Signed1), .Enable(decoder_1_out1), .Load(Load), .Store(Store),
    .Size_Flag(Size_Flag), .Address(Address[23:0]), .Clock(Clock), .Data_In(Data_In), .Data_Out(RAM1_data_out));
  RAM_Block RAM2 (
    .Unsigned0_Signed1(Unsigned0_Signed1), .Enable(decoder_1_out2), .Load(Load), .Store(Store),
    .Size_Flag(Size_Flag), .Address(Address[23:0]), .Clock(Clock), .Data_In(Data_In), .Data_Out(RAM2_data_out));
  RAM_Block RAM3 (
    .Unsigned0_Signed1(Unsigned0_Signed1), .Enable(decoder_1_out3), .Load(Load), .Store(Store),
    .Size_Flag(Size_Flag), .Address(Address[23:0]), .Clock(Clock), .Data_In(Data_In), .Data_Out(RAM3_data_out));
  RAM_Block RAM4 (
    .Unsigned0_Signed1(Unsigned0_Signed1), .Enable(decoder_1_out4), .Load(Load), .Store(Store),
    .Size_Flag(Size_Flag), .Address(Address[23:0]), .Clock(Clock), .Data_In(Data_In), .Data_Out(RAM4_data_out));
  RAM_Block RAM5 (
    .Unsigned0_Signed1(Unsigned0_Signed1), .Enable(decoder_1_out5), .Load(Load), .Store(Store),
    .Size_Flag(Size_Flag), .Address(Address[23:0]), .Clock(Clock), .Data_In(Data_In), .Data_Out(RAM5_data_out));
  RAM_Block RAM6 (
    .Unsigned0_Signed1(Unsigned0_Signed1), .Enable(decoder_1_out6), .Load(Load), .Store(Store),
    .Size_Flag(Size_Flag), .Address(Address[23:0]), .Clock(Clock), .Data_In(Data_In), .Data_Out(RAM6_data_out));
  RAM_Block RAM7 (
    .Unsigned0_Signed1(Unsigned0_Signed1), .Enable(decoder_1_out7), .Load(Load), .Store(Store),
    .Size_Flag(Size_Flag), .Address(Address[23:0]), .Clock(Clock), .Data_In(Data_In), .Data_Out(RAM7_data_out));
  RAM_Block RAM8 (
    .Unsigned0_Signed1(Unsigned0_Signed1), .Enable(decoder_1_out8), .Load(Load), .Store(Store),
    .Size_Flag(Size_Flag), .Address(Address[23:0]), .Clock(Clock), .Data_In(Data_In), .Data_Out(RAM8_data_out));
  RAM_Block RAM9 (
    .Unsigned0_Signed1(Unsigned0_Signed1), .Enable(decoder_1_out9), .Load(Load), .Store(Store),
    .Size_Flag(Size_Flag), .Address(Address[23:0]), .Clock(Clock), .Data_In(Data_In), .Data_Out(RAM9_data_out));
  RAM_Block RAM10 (
    .Unsigned0_Signed1(Unsigned0_Signed1), .Enable(decoder_1_out10), .Load(Load), .Store(Store),
    .Size_Flag(Size_Flag), .Address(Address[23:0]), .Clock(Clock), .Data_In(Data_In),
    .Data_Out(RAM10_data_out));
  RAM_Block RAM11 (
    .Unsigned0_Signed1(Unsigned0_Signed1), .Enable(decoder_1_out11), .Load(Load), .Store(Store),
    .Size_Flag(Size_Flag), .Address(Address[23:0]), .Clock(Clock), .Data_In(Data_In),
    .Data_Out(RAM11_data_out));
  RAM_Block RAM12 (
    .Unsigned0_Signed1(Unsigned0_Signed1), .Enable(decoder_1_out12), .Load(Load), .Store(Store),
    .Size_Flag(Size_Flag), .Address(Address[23:0]), .Clock(Clock), .Data_In(Data_In),
    .Data_Out(RAM12_data_out));
  RAM_Block RAM13 (
    .Unsigned0_Signed1(Unsigned0_Signed1), .Enable(decoder_1_out13), .Load(Load), .Store(Store),
    .Size_Flag(Size_Flag), .Address(Address[23:0]), .Clock(Clock), .Data_In(Data_In),
    .Data_Out(RAM13_data_out));
  RAM_Block RAM14 (
    .Unsigned0_Signed1(Unsigned0_Signed1), .Enable(decoder_1_out14), .Load(Load), .Store(Store),
    .Size_Flag(Size_Flag), .Address(Address[23:0]), .Clock(Clock), .Data_In(Data_In),
    .Data_Out(RAM14_data_out));
  RAM_Block RAM15 (
    .Unsigned0_Signed1(Unsigned0_Signed1), .Enable(decoder_1_out15), .Load(Load), .Store(Store),
    .Size_Flag(Size_Flag), .Address(Address[23:0]), .Clock(Clock), .Data_In(Data_In),
    .Data_Out(RAM15_data_out));
  Multiplexer #(.enable("true"), .select(4), .width(32)) multiplexer_1 (
    .in0(RAM0_data_out), .in1(RAM1_data_out), .in2(RAM2_data_out), .in3(RAM3_data_out), .in4(RAM4_data_out),
    .in5(RAM5_data_out), .in6(RAM6_data_out), .in7(RAM7_data_out), .in8(RAM8_data_out), .in9(RAM9_data_out),
    .in10(RAM10_data_out), .in11(RAM11_data_out), .in12(RAM12_data_out), .in13(RAM13_data_out),
    .in14(RAM14_data_out), .in15(RAM15_data_out), .out(Data_Out), .sel(Address[27:24]), .en(Load));

  // Notes on the sheet:
  //   Size Flags
  //   00 = Store/Load Byte
  //   01 = Store/Load Half Word
  //   10 = Store/Load Word
  //   2^32 addresses per byte = 4GB total
  //   Implementing the entire 4GB range is unreasonable as that requires 256 RAM blocks
  //   To make this more reasonable, I'm addressing only 16 RAM blocks (4 address bits)
endmodule

module RAM_Block (
  input  Unsigned0_Signed1,
  input  Enable,
  input  Load,
  input  Store,
  input  [1:0] Size_Flag,
  input  [23:0] Address,
  input  Clock,
  input  [31:0] Data_In,
  output [31:0] Data_Out
);

  wire and_1_out, and_2_out;
  wire [3:0] multiplexer_1_out;
  wire [7:0] Mem_Byte0_dout, Mem_Byte1_dout, Mem_Byte2_dout, Mem_Byte3_dout;
  wire [31:0] bit_extender_1_out, bit_extender_2_out;

  and and_1 (and_1_out, Enable, Load);
  and and_2 (and_2_out, Enable, Store);
  Multiplexer #(.enable("true"), .select(2), .width(4)) multiplexer_1 (
    .in0(4'b0001), .in1(4'b0011), .in2(4'b1111), .in3(4'b0000), .out(multiplexer_1_out), .sel(Size_Flag),
    .en(and_2_out));
  RAM #(.addrWidth(24)) Mem_Byte0 (
    .addr(Address), .we(multiplexer_1_out[0]), .oe(and_1_out), .clk(Clock), .din(Data_In[7:0]),
    .dout(Mem_Byte0_dout));
  RAM #(.addrWidth(24)) Mem_Byte1 (
    .addr(Address), .we(multiplexer_1_out[1]), .oe(and_1_out), .clk(Clock), .din(Data_In[15:8]),
    .dout(Mem_Byte1_dout));
  RAM #(.addrWidth(24)) Mem_Byte2 (
    .addr(Address), .we(multiplexer_1_out[2]), .oe(and_1_out), .clk(Clock), .din(Data_In[23:16]),
    .dout(Mem_Byte2_dout));
  RAM #(.addrWidth(24)) Mem_Byte3 (
    .addr(Address), .we(multiplexer_1_out[3]), .oe(and_1_out), .clk(Clock), .din(Data_In[31:24]),
    .dout(Mem_Byte3_dout));
  assign bit_extender_1_out = {{24{Unsigned0_Signed1}}, Mem_Byte0_dout};  // Bit_Extender bit_extender_1
  assign bit_extender_2_out = {{16{Unsigned0_Signed1}}, {Mem_Byte1_dout, Mem_Byte0_dout}};  // Bit_Extender bit_extender_2
  Multiplexer #(.enable("true"), .select(2), .width(32)) multiplexer_2 (
    .in0(bit_extender_1_out), .in1(bit_extender_2_out),
    .in2({Mem_Byte3_dout, Mem_Byte2_dout, Mem_Byte1_dout, Mem_Byte0_dout}), .in3({32{1'b0}}), .out(Data_Out),
    .sel(Size_Flag), .en(and_1_out));

  // Notes on the sheet:
  //   Size Flags
  //   00 = Store/Load Byte
  //   01 = Store/Load Half Word
  //   10 = Store/Load Word
  //   11 = Invalid
  //   This RAM Block handles up to 32 bits (4 bytes) per store or load.
  //   The Size Flag input determines whether to store/load a byte, half word, or full word
endmodule
